// Logisim project CPU2016.circ as structural Verilog: 14 circuits, main circuit Processor
module Processor (
  output [31:0] out_1
);

  wire branchcontrol_1_o_rjmp, clock_1_out, control_1_halt, control_1_running, controlled_buffer_1_out,
       IO_CLR, MM_R, MM_W, not_1_out, not_2_out, terminal_1_o_clk_key, terminal_1_o_clk_tty,
       terminal_1_o_en_key, terminal_1_o_en_tty;
  wire [3:0] alu_1_o_flags;
  wire [4:0] control_1_o_rd, control_1_o_rr;
  wire [6:0] keyboard_1_data, terminal_1_o_char;
  wire [7:0] bit_extender_1_out;
  wire [23:0] controlled_buffer_2_out, programcounter_1_o_addr, stackpointer_1_o_data;
  wire [31:0] control_1_o_ctrl, control_1_o_im16, control_1_o_im21, MM_1, or_1_out, portout_1_o_data,
       portout_2_o_data, ram_1_o_data, regbank_1_o_a, regbank_1_o_b;

  Pull_Resistor pull_resistor_1 (.node(out_1));
  Clock clock_1 (.out(clock_1_out));
  BranchControl branchcontrol_1 (
    .i_alu_flags(alu_1_o_flags), .o_rjmp(branchcontrol_1_o_rjmp), .i_mask(control_1_o_ctrl[19:16]),
    .i_rjmp(control_1_o_ctrl[14]), .i_not(control_1_o_ctrl[15]));
  DotMatrix #(.matrixcols(8), .matrixrows(1)) dotmatrix_1 (
    .col0(portout_1_o_data[7]), .col1(portout_1_o_data[6]), .col2(portout_1_o_data[5]),
    .col3(portout_1_o_data[4]), .col4(portout_1_o_data[3]), .col5(portout_1_o_data[2]),
    .col6(portout_1_o_data[1]), .col7(portout_1_o_data[0]));
  assign controlled_buffer_1_out = not_1_out ? control_1_o_ctrl[20] : 1'bz;  // Controlled_Buffer controlled_buffer_1
  Pull_Resistor pull_resistor_2 (.node(controlled_buffer_1_out));
  not not_1 (not_1_out, clock_1_out);
  assign controlled_buffer_2_out = controlled_buffer_1_out ? stackpointer_1_o_data : 24'bz;  // Controlled_Buffer controlled_buffer_2
  not not_2 (not_2_out, controlled_buffer_1_out);
  ProgramCounter programcounter_1 (
    .i_data(out_1), .o_addr(programcounter_1_o_addr), .o_data(out_1), .i_read(MM_R), .i_write(MM_W),
    .i_en(MM_1[2]), .i_count(control_1_o_ctrl[2]), .i_reset(IO_CLR), .i_rjmp(branchcontrol_1_o_rjmp));
  assign controlled_buffer_2_out = not_2_out ? programcounter_1_o_addr : 24'bz;  // Controlled_Buffer controlled_buffer_3
  PortOut portout_1 (
    .i_data(out_1), .o_data(portout_1_o_data), .i_write(MM_W), .i_clear(IO_CLR), .o_data_2(out_1),
    .i_read(MM_R), .i_en(MM_1[1]));
  StackPointer stackpointer_1 (
    .i_data(out_1), .o_data_2(out_1), .i_pop(control_1_o_ctrl[21]), .i_push(controlled_buffer_1_out),
    .o_data(stackpointer_1_o_data), .i_read(MM_R), .i_write(MM_W), .i_en(MM_1[4]));
  assign or_1_out = out_1 | ram_1_o_data;  // OR_Gate or_1, 32 bits wide
  LED Halted (.in(control_1_halt));
  LED Running (.in(control_1_running));
  DotMatrix #(.matrixcols(8), .matrixrows(1)) dotmatrix_2 (
    .col0(portout_2_o_data[7]), .col1(portout_2_o_data[6]), .col2(portout_2_o_data[5]),
    .col3(portout_2_o_data[4]), .col4(portout_2_o_data[3]), .col5(portout_2_o_data[2]),
    .col6(portout_2_o_data[1]), .col7(portout_2_o_data[0]));
  RAM ram_1 (.i_addr(controlled_buffer_2_out), .i_data(or_1_out), .o_data(ram_1_o_data), .i_write(control_1_o_ctrl[5]));
  assign out_1 = control_1_o_ctrl[6] ? ram_1_o_data : 32'bz;  // Controlled_Buffer controlled_buffer_4
  Pull_Resistor pull_resistor_3 (.node(ram_1_o_data));
  PortOut portout_2 (
    .i_data(out_1), .o_data(portout_2_o_data), .i_write(MM_W), .i_clear(IO_CLR), .o_data_2(out_1),
    .i_read(MM_R), .i_en(MM_1[0]));
  RegBank regbank_1 (
    .i_data(out_1), .i_Rd(control_1_o_rd), .i_write(control_1_o_ctrl[0]), .i_Rr(control_1_o_rr),
    .i_read(control_1_o_ctrl[1]), .o_a(regbank_1_o_a), .o_b(regbank_1_o_b));
  assign out_1 = control_1_o_ctrl[4] ? control_1_o_im21 : 32'bz;  // Controlled_Buffer controlled_buffer_5
  assign out_1 = control_1_o_ctrl[3] ? control_1_o_im16 : 32'bz;  // Controlled_Buffer controlled_buffer_6
  Control control_1 (
    .o_im21(control_1_o_im21), .o_im16(control_1_o_im16), .o_Rd(control_1_o_rd), .o_Rr(control_1_o_rr),
    .o_ctrl({control_1_o_ctrl[31:8], IO_CLR, control_1_o_ctrl[6:0]}), .i_instr(ram_1_o_data),
    .running(control_1_running), .halt(control_1_halt));
  TTY #(.rows(16), .cols(64)) tty_1 (
    .data(terminal_1_o_char), .clk(terminal_1_o_clk_tty), .we(terminal_1_o_en_tty));  // open: clr
  Terminal terminal_1 (
    .i_data(out_1), .o_data(out_1), .o_clk_tty(terminal_1_o_clk_tty), .o_clk_key(terminal_1_o_clk_key),
    .o_char(terminal_1_o_char), .o_en_tty(terminal_1_o_en_tty), .i_char(keyboard_1_data),
    .o_en_key(terminal_1_o_en_key), .i_read(MM_R), .i_write(MM_W), .i_en(MM_1[3]));
  ALU alu_1 (
    .i_a(regbank_1_o_a), .i_b(regbank_1_o_b), .o_data(out_1), .in_1(control_1_o_ctrl[11:8]),
    .o_flags(alu_1_o_flags));
  Bit_Extender #(.in_width(32), .out_width(8)) bit_extender_1 (.in(control_1_o_im16), .out(bit_extender_1_out));
  MemMap memmap_1 (
    .i_addr(bit_extender_1_out), .i_write(control_1_o_ctrl[12]), .i_read(control_1_o_ctrl[13]),
    .o_mmap1(MM_1), .o_mmap_write(MM_W), .o_mmap_read(MM_R));  // open: o_mmap2, o_mmap3, o_mmap4
  Keyboard keyboard_1 (
    .clk(terminal_1_o_clk_key), .re(terminal_1_o_en_key), .data(keyboard_1_data));  // open: clr, avail
endmodule

module Control (
  input  [31:0] i_instr,
  output [31:0] o_im21,
  output [31:0] o_im16,
  output [4:0] o_Rd,
  output [4:0] o_Rr,
  output [31:0] o_ctrl,
  output running,
  output halt
);

  wire clock_1_out, not_1_out, not_2_out, pull_resistor_1_node;
  wire [5:0] bit_extender_1_out;
  wire [31:0] register_1_q;

  Clock clock_1 (.out(clock_1_out));
  not not_1 (not_1_out, o_ctrl[31]);
  Pull_Resistor pull_resistor_1 (.node(pull_resistor_1_node));
  assign pull_resistor_1_node = not_1_out ? clock_1_out : 1'bz;  // Controlled_Buffer controlled_buffer_1
  not not_2 (not_2_out, pull_resistor_1_node);
  D_Flip_Flop d_ff_1 (.Q(running), .preset(clock_1_out), .reset(o_ctrl[31]));  // open: clk, D, Qn, en
  Register #(.width(32)) register_1 (.D(i_instr), .en(not_2_out), .Q(register_1_q), .clk(not_2_out));  // open: clr
  D_Flip_Flop d_ff_2 (.Q(halt), .preset(o_ctrl[31]));  // open: clk, D, Qn, en, reset
  Bit_Extender #(.in_width(32), .out_width(6)) bit_extender_1 (.in(register_1_q), .out(bit_extender_1_out));
  Bit_Extender #(.in_width(26), .out_width(10)) bit_extender_2 (.in(register_1_q[31:6]), .out({o_Rr, o_Rd}));
  ROM #(.addrWidth(6), .dataWidth(32)) rom_1 (.addr(bit_extender_1_out), .data(o_ctrl));  // open: sel
  assign o_im21 = {{11{1'b0}}, register_1_q[31:11]};  // Bit_Extender bit_extender_3
  assign o_im16 = {{16{1'b0}}, register_1_q[31:16]};  // Bit_Extender bit_extender_4

  // Notes on the sheet:
  //   contents of rom_1 (hex, n*v repeats v):
  //   4 15 7 107 207 307 407 507 607 1006 400c 4400c 4c00c 2005 7 80000000 100026 200004
endmodule

module ProgramCounter (
  input  [31:0] i_data,
  input  i_read,
  input  i_write,
  input  i_en,
  input  i_count,
  input  i_reset,
  input  i_rjmp,
  output [23:0] o_addr,
  output [31:0] o_data
);

  wire and_1_out, and_2_out, and_3_out, and_4_out, clock_1_out, not_1_out, not_2_out, not_3_out, or_1_out;
  wire [15:0] bit_extender_2_out;
  wire [23:0] adder_1_out, adder_2_out, adder_3_out, bit_extender_1_out, bit_extender_3_out,
       controlled_buffer_1_out, controlled_buffer_4_out, demultiplexer_1_out0, demultiplexer_1_out1,
       multiplexer_1_out, register_1_q, subtractor_1_out, subtractor_2_out;
  wire [31:0] bit_extender_4_out;

  Bit_Extender #(.in_width(32), .out_width(24)) bit_extender_1 (.in(i_data), .out(bit_extender_1_out));
  assign controlled_buffer_1_out = not_1_out ? bit_extender_1_out : 24'bz;  // Controlled_Buffer controlled_buffer_1
  not not_1 (not_1_out, i_rjmp);
  assign o_data = and_1_out ? bit_extender_4_out : 32'bz;  // Controlled_Buffer controlled_buffer_2
  and and_1 (and_1_out, i_read, i_en);
  Bit_Extender #(.in_width(24)) bit_extender_2 (.in(bit_extender_1_out), .out(bit_extender_2_out));
  assign controlled_buffer_1_out = i_rjmp ? controlled_buffer_4_out : 24'bz;  // Controlled_Buffer controlled_buffer_3
  Demultiplexer #(.width(24), .enable("false")) demultiplexer_1 (
    .out0(demultiplexer_1_out0), .out1(demultiplexer_1_out1), .in(bit_extender_3_out),
    .sel(bit_extender_2_out[15]));
  assign bit_extender_3_out = {{9{1'b0}}, bit_extender_2_out[14:0]};  // Bit_Extender bit_extender_3
  Adder #(.width(24)) adder_1 (.a(24'h1), .b(controlled_buffer_1_out), .out(adder_1_out));  // open: cin, cout
  or or_1 (or_1_out, and_2_out, i_rjmp);
  and and_2 (and_2_out, i_write, i_en);
  Multiplexer #(.width(24), .enable("false")) multiplexer_1 (
    .in0(adder_3_out), .in1(adder_1_out), .out(multiplexer_1_out), .sel(or_1_out));
  assign bit_extender_4_out = {{8{1'b0}}, register_1_q};  // Bit_Extender bit_extender_4
  not not_2 (not_2_out, or_1_out);
  Clock clock_1 (.out(clock_1_out));
  Adder #(.width(24)) adder_2 (.a(subtractor_2_out), .b(demultiplexer_1_out0), .out(adder_2_out));  // open: cin, cout
  assign controlled_buffer_4_out = not_3_out ? adder_2_out : 24'bz;  // Controlled_Buffer controlled_buffer_4
  not not_3 (not_3_out, bit_extender_2_out[15]);
  assign controlled_buffer_4_out = bit_extender_2_out[15] ? subtractor_1_out : 24'bz;  // Controlled_Buffer controlled_buffer_5
  Subtractor #(.width(24)) subtractor_1 (
    .a(subtractor_2_out), .b(demultiplexer_1_out1), .out(subtractor_1_out));  // open: bin, bout
  Subtractor #(.width(24)) subtractor_2 (.a(register_1_q), .b(24'h1), .out(subtractor_2_out));  // open: bin, bout
  Register #(.width(24), .trigger("falling")) register_1 (
    .D(multiplexer_1_out), .en(i_count), .Q(register_1_q), .clk(clock_1_out), .clr(i_reset));
  assign o_addr = and_3_out ? register_1_q : 24'bz;  // Controlled_Buffer controlled_buffer_6
  and and_3 (and_3_out, clock_1_out, not_2_out);
  Adder #(.width(24)) adder_3 (.a(24'h1), .b(register_1_q), .out(adder_3_out));  // open: cin, cout
  assign o_addr = and_4_out ? controlled_buffer_1_out : 24'bz;  // Controlled_Buffer controlled_buffer_7
  and and_4 (and_4_out, or_1_out, clock_1_out);
endmodule

module Prototype (
);

  wire clock_1_out, not_1_out, not_2_out;
  wire [7:0] register_1_q;
  wire [23:0] controlled_buffer_1_out, counter_1_q, pull_resistor_1_node, pull_resistor_3_node,
       register_1_q_2;
  wire [31:0] bit_extender_1_out, controlled_buffer_6_out, or_1_out, pull_resistor_2_node, ram_1_data,
       register_2_q, register_3_q, register_4_q, register_5_q, rom_1_data;

  Clock clock_1 (.out(clock_1_out));
  not not_1 (not_1_out, clock_1_out);
  Counter #(.width(24), .max('hffffff), .trigger("falling")) counter_1 (
    .count(1'b1), .Q(counter_1_q), .clk(clock_1_out));  // open: load, D, carry, clr
  assign controlled_buffer_1_out = clock_1_out ? counter_1_q : 24'bz;  // Controlled_Buffer controlled_buffer_1
  assign controlled_buffer_1_out = not_1_out ? pull_resistor_1_node : 24'bz;  // Controlled_Buffer controlled_buffer_2
  ROM #(.dataWidth(32)) rom_1 (.addr(register_1_q), .data(rom_1_data));  // open: sel
  Pull_Resistor pull_resistor_1 (.node(pull_resistor_1_node));
  Pull_Resistor pull_resistor_2 (.node(pull_resistor_2_node));
  assign pull_resistor_2_node = not_2_out ? ram_1_data : 32'bz;  // Controlled_Buffer controlled_buffer_3
  not not_2 (not_2_out, rom_1_data[10]);
  RAM_part #(.addrWidth(24), .dataWidth(32), .bus("separate")) ram_1 (
    .addr(controlled_buffer_1_out), .din(controlled_buffer_6_out), .data(ram_1_data), .str(rom_1_data[0]),
    .clk(clock_1_out));  // open: sel, ld, clr
  assign bit_extender_1_out = {{8{1'b0}}, pull_resistor_3_node};  // Bit_Extender bit_extender_1
  Pull_Resistor pull_resistor_3 (.node(pull_resistor_3_node));
  assign pull_resistor_3_node = rom_1_data[10] ? register_1_q_2 : 24'bz;  // Controlled_Buffer controlled_buffer_4
  Register #(.width(32)) register_1 (
    .D(ram_1_data), .en(not_1_out), .Q({register_1_q_2, register_1_q}), .clk(not_1_out));  // open: clr
  assign pull_resistor_1_node = rom_1_data[1] ? register_1_q_2 : 24'bz;  // Controlled_Buffer controlled_buffer_5
  assign or_1_out = pull_resistor_2_node | bit_extender_1_out;  // OR_Gate or_1, 32 bits wide
  Register #(.width(32)) register_2 (.D(or_1_out), .en(rom_1_data[2]), .Q(register_2_q), .clk(not_1_out));  // open: clr
  Register #(.width(32)) register_3 (.D(or_1_out), .en(rom_1_data[3]), .Q(register_3_q), .clk(not_1_out));  // open: clr
  Register #(.width(32)) register_4 (.D(or_1_out), .en(rom_1_data[4]), .Q(register_4_q), .clk(not_1_out));  // open: clr
  Register #(.width(32)) register_5 (.D(or_1_out), .en(rom_1_data[5]), .Q(register_5_q), .clk(not_1_out));  // open: clr
  assign controlled_buffer_6_out = rom_1_data[6] ? register_2_q : 32'bz;  // Controlled_Buffer controlled_buffer_6
  assign controlled_buffer_6_out = rom_1_data[7] ? register_3_q : 32'bz;  // Controlled_Buffer controlled_buffer_7
  assign controlled_buffer_6_out = rom_1_data[8] ? register_4_q : 32'bz;  // Controlled_Buffer controlled_buffer_8
  assign controlled_buffer_6_out = rom_1_data[9] ? register_5_q : 32'bz;  // Controlled_Buffer controlled_buffer_9

  // Notes on the sheet:
  //   contents of rom_1 (hex, n*v repeats v):
  //   0 404 408 410 420
endmodule

module RegBank (
  input  [31:0] i_data,
  input  [4:0] i_Rd,
  input  i_write,
  input  [4:0] i_Rr,
  input  i_read,
  output [31:0] o_a,
  output [31:0] o_b
);

  wire clock_1_out, decoder_1_out0, decoder_1_out1, decoder_1_out2, decoder_1_out3, decoder_1_out4,
       decoder_1_out5, decoder_1_out6, decoder_1_out7, decoder_1_out8, decoder_1_out9, decoder_1_out10,
       decoder_1_out11, decoder_1_out12, decoder_1_out13, decoder_1_out14, decoder_1_out15, decoder_1_out16,
       decoder_1_out17, decoder_1_out18, decoder_1_out19, decoder_1_out20, decoder_1_out21, decoder_1_out22,
       decoder_1_out23, decoder_1_out24, decoder_1_out25, decoder_1_out26, decoder_1_out27, decoder_1_out28,
       decoder_1_out29, decoder_1_out30, decoder_1_out31;
  wire [31:0] register_1_q, register_2_q, register_3_q, register_4_q, register_5_q, register_6_q,
       register_7_q, register_8_q, register_9_q, register_10_q, register_11_q, register_12_q, register_13_q,
       register_14_q, register_15_q, register_16_q, register_17_q, register_18_q, register_19_q,
       register_20_q, register_21_q, register_22_q, register_23_q, register_24_q, register_25_q,
       register_26_q, register_27_q, register_28_q, register_29_q, register_30_q, register_31_q,
       register_32_q;

  Decoder #(.select(5), .disabled(0)) decoder_1 (
    .out0(decoder_1_out0), .out1(decoder_1_out1), .out2(decoder_1_out2), .out3(decoder_1_out3),
    .out4(decoder_1_out4), .out5(decoder_1_out5), .out6(decoder_1_out6), .out7(decoder_1_out7),
    .out8(decoder_1_out8), .out9(decoder_1_out9), .out10(decoder_1_out10), .out11(decoder_1_out11),
    .out12(decoder_1_out12), .out13(decoder_1_out13), .out14(decoder_1_out14), .out15(decoder_1_out15),
    .out16(decoder_1_out16), .out17(decoder_1_out17), .out18(decoder_1_out18), .out19(decoder_1_out19),
    .out20(decoder_1_out20), .out21(decoder_1_out21), .out22(decoder_1_out22), .out23(decoder_1_out23),
    .out24(decoder_1_out24), .out25(decoder_1_out25), .out26(decoder_1_out26), .out27(decoder_1_out27),
    .out28(decoder_1_out28), .out29(decoder_1_out29), .out30(decoder_1_out30), .out31(decoder_1_out31),
    .sel(i_Rd), .en(i_write));
  Clock clock_1 (.out(clock_1_out));
  Register #(.width(32)) register_1 (
    .D(i_data), .en(decoder_1_out1), .Q(register_1_q), .clk(clock_1_out));  // open: clr
  Register #(.width(32)) register_2 (
    .D(i_data), .en(decoder_1_out0), .Q(register_2_q), .clk(clock_1_out));  // open: clr
  Register #(.width(32)) register_3 (
    .D(i_data), .en(decoder_1_out8), .Q(register_3_q), .clk(clock_1_out));  // open: clr
  Register #(.width(32)) register_4 (
    .D(i_data), .en(decoder_1_out9), .Q(register_4_q), .clk(clock_1_out));  // open: clr
  Register #(.width(32)) register_5 (
    .D(i_data), .en(decoder_1_out16), .Q(register_5_q), .clk(clock_1_out));  // open: clr
  Register #(.width(32)) register_6 (
    .D(i_data), .en(decoder_1_out17), .Q(register_6_q), .clk(clock_1_out));  // open: clr
  Register #(.width(32)) register_7 (
    .D(i_data), .en(decoder_1_out24), .Q(register_7_q), .clk(clock_1_out));  // open: clr
  Register #(.width(32)) register_8 (
    .D(i_data), .en(decoder_1_out25), .Q(register_8_q), .clk(clock_1_out));  // open: clr
  Register #(.width(32)) register_9 (
    .D(i_data), .en(decoder_1_out3), .Q(register_9_q), .clk(clock_1_out));  // open: clr
  Register #(.width(32)) register_10 (
    .D(i_data), .en(decoder_1_out2), .Q(register_10_q), .clk(clock_1_out));  // open: clr
  Register #(.width(32)) register_11 (
    .D(i_data), .en(decoder_1_out11), .Q(register_11_q), .clk(clock_1_out));  // open: clr
  Register #(.width(32)) register_12 (
    .D(i_data), .en(decoder_1_out10), .Q(register_12_q), .clk(clock_1_out));  // open: clr
  Register #(.width(32)) register_13 (
    .D(i_data), .en(decoder_1_out19), .Q(register_13_q), .clk(clock_1_out));  // open: clr
  Register #(.width(32)) register_14 (
    .D(i_data), .en(decoder_1_out18), .Q(register_14_q), .clk(clock_1_out));  // open: clr
  Register #(.width(32)) register_15 (
    .D(i_data), .en(decoder_1_out26), .Q(register_15_q), .clk(clock_1_out));  // open: clr
  Register #(.width(32)) register_16 (
    .D(i_data), .en(decoder_1_out27), .Q(register_16_q), .clk(clock_1_out));  // open: clr
  Register #(.width(32)) register_17 (
    .D(i_data), .en(decoder_1_out4), .Q(register_17_q), .clk(clock_1_out));  // open: clr
  Register #(.width(32)) register_18 (
    .D(i_data), .en(decoder_1_out5), .Q(register_18_q), .clk(clock_1_out));  // open: clr
  Register #(.width(32)) register_19 (
    .D(i_data), .en(decoder_1_out12), .Q(register_19_q), .clk(clock_1_out));  // open: clr
  Register #(.width(32)) register_20 (
    .D(i_data), .en(decoder_1_out13), .Q(register_20_q), .clk(clock_1_out));  // open: clr
  Register #(.width(32)) register_21 (
    .D(i_data), .en(decoder_1_out21), .Q(register_21_q), .clk(clock_1_out));  // open: clr
  Register #(.width(32)) register_22 (
    .D(i_data), .en(decoder_1_out20), .Q(register_22_q), .clk(clock_1_out));  // open: clr
  Register #(.width(32)) register_23 (
    .D(i_data), .en(decoder_1_out29), .Q(register_23_q), .clk(clock_1_out));  // open: clr
  Register #(.width(32)) register_24 (
    .D(i_data), .en(decoder_1_out28), .Q(register_24_q), .clk(clock_1_out));  // open: clr
  Register #(.width(32)) register_25 (
    .D(i_data), .en(decoder_1_out7), .Q(register_25_q), .clk(clock_1_out));  // open: clr
  Register #(.width(32)) register_26 (
    .D(i_data), .en(decoder_1_out6), .Q(register_26_q), .clk(clock_1_out));  // open: clr
  Register #(.width(32)) register_27 (
    .D(i_data), .en(decoder_1_out15), .Q(register_27_q), .clk(clock_1_out));  // open: clr
  Register #(.width(32)) register_28 (
    .D(i_data), .en(decoder_1_out14), .Q(register_28_q), .clk(clock_1_out));  // open: clr
  Register #(.width(32)) register_29 (
    .D(i_data), .en(decoder_1_out23), .Q(register_29_q), .clk(clock_1_out));  // open: clr
  Register #(.width(32)) register_30 (
    .D(i_data), .en(decoder_1_out22), .Q(register_30_q), .clk(clock_1_out));  // open: clr
  Register #(.width(32)) register_31 (
    .D(i_data), .en(decoder_1_out31), .Q(register_31_q), .clk(clock_1_out));  // open: clr
  Register #(.width(32)) register_32 (
    .D(i_data), .en(decoder_1_out30), .Q(register_32_q), .clk(clock_1_out));  // open: clr
  Multiplexer #(.select(5), .width(32)) multiplexer_1 (
    .in0(register_2_q), .in1(register_1_q), .in2(register_10_q), .in3(register_9_q), .in4(register_17_q),
    .in5(register_18_q), .in6(register_26_q), .in7(register_25_q), .in8(register_3_q), .in9(register_4_q),
    .in10(register_12_q), .in11(register_11_q), .in12(register_19_q), .in13(register_20_q),
    .in14(register_28_q), .in15(register_27_q), .in16(register_5_q), .in17(register_6_q),
    .in18(register_14_q), .in19(register_13_q), .in20(register_22_q), .in21(register_21_q),
    .in22(register_30_q), .in23(register_29_q), .in24(register_7_q), .in25(register_8_q),
    .in26(register_15_q), .in27(register_16_q), .in28(register_24_q), .in29(register_23_q),
    .in30(register_32_q), .in31(register_31_q), .out(o_b), .sel(i_Rd), .en(i_read));
  Multiplexer #(.select(5), .width(32)) multiplexer_2 (
    .in0(register_2_q), .in1(register_1_q), .in2(register_10_q), .in3(register_9_q), .in4(register_17_q),
    .in5(register_18_q), .in6(register_26_q), .in7(register_25_q), .in8(register_3_q), .in9(register_4_q),
    .in10(register_12_q), .in11(register_11_q), .in12(register_19_q), .in13(register_20_q),
    .in14(register_28_q), .in15(register_27_q), .in16(register_5_q), .in17(register_6_q),
    .in18(register_14_q), .in19(register_13_q), .in20(register_22_q), .in21(register_21_q),
    .in22(register_30_q), .in23(register_29_q), .in24(register_7_q), .in25(register_8_q),
    .in26(register_15_q), .in27(register_16_q), .in28(register_24_q), .in29(register_23_q),
    .in30(register_32_q), .in31(register_31_q), .out(o_a), .sel(i_Rr), .en(i_read));
endmodule

module RAM (
  input  [23:0] i_addr,
  input  [31:0] i_data,
  input  i_write,
  output [31:0] o_data
);

  wire clock_1_out;

  Clock clock_1 (.out(clock_1_out));
  RAM_part #(.addrWidth(24), .dataWidth(32), .bus("separate")) ram_1 (
    .addr(i_addr), .din(i_data), .data(o_data), .str(i_write), .clk(clock_1_out));  // open: sel, ld, clr
endmodule

// 2
module ALU (
  input  [3:0] in_1,
  input  [31:0] i_a,
  input  [31:0] i_b,
  output [31:0] o_data,
  output [3:0] o_flags
);

  wire clock_1_out, decoder_1_out0, decoder_1_out1, decoder_1_out2, decoder_1_out3, decoder_1_out4,
       decoder_1_out5, decoder_1_out6;
  wire [3:0] adder_1_cout;
  wire [4:0] bit_extender_1_out;
  wire [31:0] adder_1_out, divider_1_out, multiplier_1_out, negator_1_out, shifter_1_out, subtractor_1_out;

  Adder #(.width(32)) adder_1 (.a(i_a), .b(i_b), .out(adder_1_out), .cout(adder_1_cout[0]));  // open: cin
  Subtractor #(.width(32)) subtractor_1 (.a(i_b), .b(i_a), .out(subtractor_1_out));  // open: bin, bout
  Multiplier #(.width(32)) multiplier_1 (.a(i_a), .b(i_b), .out(multiplier_1_out));  // open: cin, cout
  Divider #(.width(32)) divider_1 (.a(i_a), .b(i_b), .out(divider_1_out));  // open: upper, rem
  Negator #(.width(32)) negator_1 (.in(i_a), .out(negator_1_out));
  Bit_Extender #(.in_width(32), .out_width(5)) bit_extender_1 (.in(i_b), .out(bit_extender_1_out));
  Decoder #(.select(4)) decoder_1 (
    .out0(decoder_1_out0), .out1(decoder_1_out1), .out2(decoder_1_out2), .out3(decoder_1_out3),
    .out4(decoder_1_out4), .out5(decoder_1_out5), .out6(decoder_1_out6), .sel(in_1));  // open: out7, out8, out9, out10, out11, out12, out13, out14, out15, en
  assign o_data = decoder_1_out0 ? i_a : 32'bz;  // Controlled_Buffer controlled_buffer_1
  assign o_data = decoder_1_out1 ? adder_1_out : 32'bz;  // Controlled_Buffer controlled_buffer_2
  assign o_data = decoder_1_out2 ? subtractor_1_out : 32'bz;  // Controlled_Buffer controlled_buffer_3
  assign o_data = decoder_1_out3 ? multiplier_1_out : 32'bz;  // Controlled_Buffer controlled_buffer_4
  assign o_data = decoder_1_out4 ? divider_1_out : 32'bz;  // Controlled_Buffer controlled_buffer_5
  assign o_data = decoder_1_out5 ? negator_1_out : 32'bz;  // Controlled_Buffer controlled_buffer_6
  Shifter #(.width(32)) shifter_1 (.in(i_a), .\dist (bit_extender_1_out), .out(shifter_1_out));
  assign o_data = decoder_1_out6 ? shifter_1_out : 32'bz;  // Controlled_Buffer controlled_buffer_7
  Comparator #(.width(32), .mode("unsigned")) comparator_1 (
    .a(o_data), .b({32{1'b0}}), .gt(adder_1_cout[1]), .eq(adder_1_cout[2]), .lt(adder_1_cout[3]));
  Clock clock_1 (.out(clock_1_out));
  Register #(.width(4)) register_1 (.D(adder_1_cout), .en(clock_1_out), .Q(o_flags), .clk(clock_1_out));  // open: clr
endmodule

module PortOut (
  input  [31:0] i_data,
  input  i_read,
  input  i_write,
  input  i_clear,
  input  i_en,
  output [31:0] o_data,
  output [31:0] o_data_2
);

  wire clock_1_out, pull_resistor_1_node, pull_resistor_2_node;

  assign o_data_2 = pull_resistor_1_node ? i_data : 32'bz;  // Controlled_Buffer controlled_buffer_1
  Pull_Resistor pull_resistor_1 (.node(pull_resistor_1_node));
  assign pull_resistor_1_node = i_en ? i_read : 1'bz;  // Controlled_Buffer controlled_buffer_2
  Pull_Resistor pull_resistor_2 (.node(pull_resistor_2_node));
  assign pull_resistor_2_node = i_en ? i_write : 1'bz;  // Controlled_Buffer controlled_buffer_3
  Clock clock_1 (.out(clock_1_out));
  Register #(.width(32)) register_1 (
    .D(i_data), .en(pull_resistor_2_node), .Q(o_data), .clk(clock_1_out), .clr(i_clear));
endmodule

module MemMap (
  input  [7:0] i_addr,
  input  i_write,
  input  i_read,
  output [31:0] o_mmap1,
  output [31:0] o_mmap2,
  output [31:0] o_mmap3,
  output [31:0] o_mmap4,
  output o_mmap_write,
  output o_mmap_read
);

  ROM #(.dataWidth(32)) rom_1 (.addr(i_addr), .data(o_mmap1));  // open: sel
  ROM #(.dataWidth(32)) rom_2 (.addr(i_addr), .data(o_mmap2));  // open: sel
  ROM #(.dataWidth(32)) rom_3 (.addr(i_addr), .data(o_mmap3));  // open: sel
  ROM #(.dataWidth(32)) rom_4 (.addr(i_addr), .data(o_mmap4));  // open: sel

  assign o_mmap_read = i_read;
  assign o_mmap_write = i_write;

  // Notes on the sheet:
  //   contents of rom_1 (hex, n*v repeats v):
  //   1 2 4 8 10 20 40 80 100 200 400 800 1000 2000 4000 8000 10000 20000 40000 80000 100000 200000 400000
  //   800000 1000000 2000000 4000000 8000000 10000000 20000000 40000000 80000000
  //   contents of rom_2 (hex, n*v repeats v):
  //   32*0 1 2 4 8 10 20 40 80 100 200 400 800 1000 2000 4000 8000 10000 20000 40000 80000 100000 200000
  //   400000 800000 1000000 2000000 4000000 8000000 10000000 20000000 40000000 80000000
endmodule

module Counter32 (
  input  [31:0] i_data,
  input  i_read,
  input  i_write,
  input  i_en,
  input  i_clear,
  output [31:0] o_data
);

  wire clock_1_out, pull_resistor_1_node, pull_resistor_2_node, undriven;
  wire [31:0] counter_1_q;

  assign o_data = pull_resistor_2_node ? counter_1_q : 32'bz;  // Controlled_Buffer controlled_buffer_1
  Pull_Resistor pull_resistor_1 (.node(pull_resistor_1_node));
  Pull_Resistor pull_resistor_2 (.node(pull_resistor_2_node));
  assign pull_resistor_1_node = i_en ? i_write : 1'bz;  // Controlled_Buffer controlled_buffer_2
  assign pull_resistor_2_node = i_en ? i_read : 1'bz;  // Controlled_Buffer controlled_buffer_3
  Clock clock_1 (.out(clock_1_out));
  Counter #(.width(32), .max('hffffffff)) counter_1 (
    .load(pull_resistor_1_node), .D(i_data), .count(undriven), .Q(counter_1_q), .clk(clock_1_out),
    .clr(i_clear));  // open: carry
endmodule

module mmReg (
  input  [31:0] i_data,
  input  i_read,
  input  i_write,
  input  i_clear,
  input  i_en,
  output [31:0] o_data,
  output [31:0] o_data_2
);

  wire clock_1_out, pull_resistor_1_node, pull_resistor_2_node;

  assign o_data_2 = pull_resistor_1_node ? o_data : 32'bz;  // Controlled_Buffer controlled_buffer_1
  Pull_Resistor pull_resistor_1 (.node(pull_resistor_1_node));
  assign pull_resistor_1_node = i_en ? i_read : 1'bz;  // Controlled_Buffer controlled_buffer_2
  Register #(.width(32)) register_1 (
    .D(i_data), .en(pull_resistor_2_node), .Q(o_data), .clk(clock_1_out), .clr(i_clear));
  Clock clock_1 (.out(clock_1_out));
  Pull_Resistor pull_resistor_2 (.node(pull_resistor_2_node));
  assign pull_resistor_2_node = i_en ? i_write : 1'bz;  // Controlled_Buffer controlled_buffer_3
endmodule

module BranchControl (
  input  [3:0] i_alu_flags,
  input  [3:0] i_mask,
  input  i_rjmp,
  input  i_not,
  output o_rjmp
);

  wire comparator_1_eq, not_1_out;
  wire [3:0] and_1_out, controlled_buffer_1_out, not_2_out;

  assign and_1_out = controlled_buffer_1_out & i_mask;  // AND_Gate and_1, 4 bits wide
  and and_2 (o_rjmp, i_rjmp, comparator_1_eq);
  Comparator #(.width(4), .mode("unsigned")) comparator_1 (
    .a(and_1_out), .b(i_mask), .eq(comparator_1_eq));  // open: gt, lt
  assign controlled_buffer_1_out = not_1_out ? i_alu_flags : 4'bz;  // Controlled_Buffer controlled_buffer_1
  not not_1 (not_1_out, i_not);
  assign not_2_out = ~i_alu_flags;  // NOT_Gate not_2, 4 bits wide
  assign controlled_buffer_1_out = i_not ? not_2_out : 4'bz;  // Controlled_Buffer controlled_buffer_2
endmodule

module Terminal (
  input  [31:0] i_data,
  input  [6:0] i_char,
  input  i_read,
  input  i_write,
  input  i_en,
  output o_clk_tty,
  output o_clk_key,
  output [6:0] o_char,
  output o_en_tty,
  output [31:0] o_data,
  output o_en_key
);

  wire [31:0] bit_extender_2_out;

  Clock clock_1 (.out(o_clk_key));
  Bit_Extender #(.in_width(32), .out_width(7)) bit_extender_1 (.in(i_data), .out(o_char));
  assign o_data = o_en_key ? bit_extender_2_out : 32'bz;  // Controlled_Buffer controlled_buffer_1
  Pull_Resistor pull_resistor_1 (.node(o_en_tty));
  Pull_Resistor pull_resistor_2 (.node(o_en_key));
  assign o_en_key = i_en ? i_read : 1'bz;  // Controlled_Buffer controlled_buffer_2
  assign o_en_tty = i_en ? i_write : 1'bz;  // Controlled_Buffer controlled_buffer_3
  assign bit_extender_2_out = {{25{1'b0}}, i_char};  // Bit_Extender bit_extender_2
  Pull_Resistor pull_resistor_3 (.node(i_char));
  TTY tty_1 ();  // open: data, clk, we, clr
  Keyboard keyboard_1 ();  // open: clk, re, clr, avail, data

  assign o_clk_tty = o_clk_key;
endmodule

module StackPointer (
  input  [31:0] i_data,
  input  i_pop,
  input  i_push,
  input  i_read,
  input  i_write,
  input  i_en,
  output [23:0] o_data,
  output [31:0] o_data_2
);

  wire clock_1_out, not_1_out, or_1_out, or_3_out, pull_resistor_3_node, pull_resistor_4_node;
  wire [23:0] adder_1_out, bit_extender_1_out, controlled_buffer_1_out, or_2_out, pull_resistor_1_node,
       subtractor_1_out;
  wire [31:0] bit_extender_2_out;

  Pull_Resistor pull_resistor_1 (.node(pull_resistor_1_node));
  assign controlled_buffer_1_out = not_1_out ? bit_extender_1_out : 24'bz;  // Controlled_Buffer controlled_buffer_1
  Pull_Resistor pull_resistor_2 (.node(controlled_buffer_1_out));
  Bit_Extender #(.in_width(32), .out_width(24)) bit_extender_1 (.in(i_data), .out(bit_extender_1_out));
  not not_1 (not_1_out, or_1_out);
  or or_1 (or_1_out, i_push, i_pop);
  assign o_data_2 = pull_resistor_3_node ? bit_extender_2_out : 32'bz;  // Controlled_Buffer controlled_buffer_2
  Pull_Resistor pull_resistor_3 (.node(pull_resistor_3_node));
  assign pull_resistor_3_node = i_en ? i_read : 1'bz;  // Controlled_Buffer controlled_buffer_3
  assign or_2_out = pull_resistor_1_node | controlled_buffer_1_out;  // OR_Gate or_2, 24 bits wide
  Register #(.width(24)) register_1 (.D(or_2_out), .en(or_3_out), .Q(o_data), .clk(clock_1_out));  // open: clr
  or or_3 (or_3_out, i_push, i_pop, pull_resistor_4_node);
  Clock clock_1 (.out(clock_1_out));
  Pull_Resistor pull_resistor_4 (.node(pull_resistor_4_node));
  assign pull_resistor_4_node = i_en ? i_write : 1'bz;  // Controlled_Buffer controlled_buffer_4
  assign bit_extender_2_out = {{8{1'b0}}, o_data};  // Bit_Extender bit_extender_2
  Adder #(.width(24)) adder_1 (.a(o_data), .b(24'h1), .out(adder_1_out));  // open: cin, cout
  assign pull_resistor_1_node = i_pop ? adder_1_out : 24'bz;  // Controlled_Buffer controlled_buffer_5
  Subtractor #(.width(24)) subtractor_1 (.a(o_data), .b(24'h1), .out(subtractor_1_out));  // open: bin, bout
  assign pull_resistor_1_node = i_push ? subtractor_1_out : 24'bz;  // Controlled_Buffer controlled_buffer_6
endmodule
